// Logisim project Digital Clock.circ as structural Verilog: 3 circuits, main circuit main
module main (
);

  wire and_1_out, and_2_out, and_3_out, and_4_out, and_5_out, and_6_out, clock_1_out, H_out,
       led_decoder_1_o1, led_decoder_1_o2, led_decoder_1_o3, led_decoder_1_o5, led_decoder_1_o6,
       led_decoder_1_o7, led_decoder_1_o8, led_decoder_2_o1, led_decoder_2_o2, led_decoder_2_o3,
       led_decoder_2_o5, led_decoder_2_o6, led_decoder_2_o7, led_decoder_2_o8, led_decoder_3_o1,
       led_decoder_3_o2, led_decoder_3_o3, led_decoder_3_o5, led_decoder_3_o6, led_decoder_3_o7,
       led_decoder_3_o8, led_decoder_4_o1, led_decoder_4_o2, led_decoder_4_o3, led_decoder_4_o5,
       led_decoder_4_o6, led_decoder_4_o7, led_decoder_4_o8, led_decoder_5_o1, led_decoder_5_o2,
       led_decoder_5_o3, led_decoder_5_o5, led_decoder_5_o6, led_decoder_5_o7, led_decoder_5_o8,
       led_decoder_6_o1, led_decoder_6_o2, led_decoder_6_o3, led_decoder_6_o5, led_decoder_6_o6,
       led_decoder_6_o7, led_decoder_6_o8, M_out, n4_bit_counter_1_q0, n4_bit_counter_1_q1,
       n4_bit_counter_1_q2, n4_bit_counter_1_q3, n4_bit_counter_2_q0, n4_bit_counter_2_q1,
       n4_bit_counter_2_q2, n4_bit_counter_2_q3, n4_bit_counter_3_q0, n4_bit_counter_3_q1,
       n4_bit_counter_3_q2, n4_bit_counter_3_q3, n4_bit_counter_4_q0, n4_bit_counter_4_q1,
       n4_bit_counter_4_q2, n4_bit_counter_4_q3, n4_bit_counter_5_q0, n4_bit_counter_5_q1,
       n4_bit_counter_5_q2, n4_bit_counter_5_q3, n4_bit_counter_6_q0, n4_bit_counter_6_q1,
       n4_bit_counter_6_q2, n4_bit_counter_6_q3, or_1_out, or_2_out, or_3_out;

  and and_1 (and_1_out, n4_bit_counter_2_q2, n4_bit_counter_1_q1);
  _7_Segment_Display u_7_segment_display_1 (
    .g(led_decoder_1_o5), .f(led_decoder_1_o6), .a(led_decoder_1_o7), .b(led_decoder_1_o8),
    .e(led_decoder_1_o1), .d(led_decoder_1_o2), .c(led_decoder_1_o3));  // open: dp
  LED_decoder led_decoder_1 (
    .I4(n4_bit_counter_1_q3), .I3(n4_bit_counter_1_q2), .I2(n4_bit_counter_1_q1), .I1(n4_bit_counter_1_q0),
    .o1(led_decoder_1_o1), .o2(led_decoder_1_o2), .o3(led_decoder_1_o3), .o5(led_decoder_1_o5),
    .o6(led_decoder_1_o6), .o7(led_decoder_1_o7), .o8(led_decoder_1_o8));
  _4_bit_counter u_4_bit_counter_1 (
    .T__Toggle(and_2_out), .Reset(and_1_out), .Q3(n4_bit_counter_1_q3), .Q2(n4_bit_counter_1_q2),
    .Q1(n4_bit_counter_1_q1), .Q0(n4_bit_counter_1_q0));
  and and_2 (and_2_out, n4_bit_counter_2_q3, n4_bit_counter_2_q1);
  _7_Segment_Display u_7_segment_display_2 (
    .g(led_decoder_2_o5), .f(led_decoder_2_o6), .a(led_decoder_2_o7), .b(led_decoder_2_o8),
    .e(led_decoder_2_o1), .d(led_decoder_2_o2), .c(led_decoder_2_o3));  // open: dp
  LED_decoder led_decoder_2 (
    .I4(n4_bit_counter_2_q3), .I3(n4_bit_counter_2_q2), .I2(n4_bit_counter_2_q1), .I1(n4_bit_counter_2_q0),
    .o1(led_decoder_2_o1), .o2(led_decoder_2_o2), .o3(led_decoder_2_o3), .o5(led_decoder_2_o5),
    .o6(led_decoder_2_o6), .o7(led_decoder_2_o7), .o8(led_decoder_2_o8));
  _4_bit_counter u_4_bit_counter_2 (
    .T__Toggle(or_1_out), .Reset(or_2_out), .Q3(n4_bit_counter_2_q3), .Q2(n4_bit_counter_2_q2),
    .Q1(n4_bit_counter_2_q1), .Q0(n4_bit_counter_2_q0));
  or or_1 (or_1_out, and_3_out, H_out);
  or or_2 (or_2_out, and_2_out, and_1_out);
  LED led_1 (.in(clock_1_out));
  LED led_2 (.in(clock_1_out));
  and and_3 (and_3_out, n4_bit_counter_3_q2, n4_bit_counter_3_q1);
  _7_Segment_Display u_7_segment_display_3 (
    .g(led_decoder_3_o5), .f(led_decoder_3_o6), .a(led_decoder_3_o7), .b(led_decoder_3_o8),
    .e(led_decoder_3_o1), .d(led_decoder_3_o2), .c(led_decoder_3_o3));  // open: dp
  LED_decoder led_decoder_3 (
    .I4(n4_bit_counter_3_q3), .I3(n4_bit_counter_3_q2), .I2(n4_bit_counter_3_q1), .I1(n4_bit_counter_3_q0),
    .o1(led_decoder_3_o1), .o2(led_decoder_3_o2), .o3(led_decoder_3_o3), .o5(led_decoder_3_o5),
    .o6(led_decoder_3_o6), .o7(led_decoder_3_o7), .o8(led_decoder_3_o8));
  _4_bit_counter u_4_bit_counter_3 (
    .T__Toggle(and_4_out), .Reset(and_3_out), .Q3(n4_bit_counter_3_q3), .Q2(n4_bit_counter_3_q2),
    .Q1(n4_bit_counter_3_q1), .Q0(n4_bit_counter_3_q0));
  _7_Segment_Display u_7_segment_display_4 (
    .g(led_decoder_4_o5), .f(led_decoder_4_o6), .a(led_decoder_4_o7), .b(led_decoder_4_o8),
    .e(led_decoder_4_o1), .d(led_decoder_4_o2), .c(led_decoder_4_o3));  // open: dp
  LED_decoder led_decoder_4 (
    .I4(n4_bit_counter_4_q3), .I3(n4_bit_counter_4_q2), .I2(n4_bit_counter_4_q1), .I1(n4_bit_counter_4_q0),
    .o1(led_decoder_4_o1), .o2(led_decoder_4_o2), .o3(led_decoder_4_o3), .o5(led_decoder_4_o5),
    .o6(led_decoder_4_o6), .o7(led_decoder_4_o7), .o8(led_decoder_4_o8));
  and and_4 (and_4_out, n4_bit_counter_4_q3, n4_bit_counter_4_q1);
  _4_bit_counter u_4_bit_counter_4 (
    .T__Toggle(or_3_out), .Reset(and_4_out), .Q3(n4_bit_counter_4_q3), .Q2(n4_bit_counter_4_q2),
    .Q1(n4_bit_counter_4_q1), .Q0(n4_bit_counter_4_q0));
  or or_3 (or_3_out, and_5_out, M_out);
  _7_Segment_Display u_7_segment_display_5 (
    .g(led_decoder_5_o5), .f(led_decoder_5_o6), .a(led_decoder_5_o7), .b(led_decoder_5_o8),
    .e(led_decoder_5_o1), .d(led_decoder_5_o2), .c(led_decoder_5_o3));  // open: dp
  LED led_3 (.in(clock_1_out));
  LED led_4 (.in(clock_1_out));
  LED_decoder led_decoder_5 (
    .I4(n4_bit_counter_5_q3), .I3(n4_bit_counter_5_q2), .I2(n4_bit_counter_5_q1), .I1(n4_bit_counter_5_q0),
    .o1(led_decoder_5_o1), .o2(led_decoder_5_o2), .o3(led_decoder_5_o3), .o5(led_decoder_5_o5),
    .o6(led_decoder_5_o6), .o7(led_decoder_5_o7), .o8(led_decoder_5_o8));
  and and_5 (and_5_out, n4_bit_counter_5_q2, n4_bit_counter_5_q1);
  _4_bit_counter u_4_bit_counter_5 (
    .T__Toggle(and_6_out), .Reset(and_5_out), .Q3(n4_bit_counter_5_q3), .Q2(n4_bit_counter_5_q2),
    .Q1(n4_bit_counter_5_q1), .Q0(n4_bit_counter_5_q0));
  Button M (.out(M_out));
  Button H (.out(H_out));
  and and_6 (and_6_out, n4_bit_counter_6_q3, n4_bit_counter_6_q1);
  Clock clock_1 (.out(clock_1_out));
  _7_Segment_Display u_7_segment_display_6 (
    .g(led_decoder_6_o5), .f(led_decoder_6_o6), .a(led_decoder_6_o7), .b(led_decoder_6_o8),
    .e(led_decoder_6_o1), .d(led_decoder_6_o2), .c(led_decoder_6_o3));  // open: dp
  LED_decoder led_decoder_6 (
    .I4(n4_bit_counter_6_q3), .I3(n4_bit_counter_6_q2), .I2(n4_bit_counter_6_q1), .I1(n4_bit_counter_6_q0),
    .o1(led_decoder_6_o1), .o2(led_decoder_6_o2), .o3(led_decoder_6_o3), .o5(led_decoder_6_o5),
    .o6(led_decoder_6_o6), .o7(led_decoder_6_o7), .o8(led_decoder_6_o8));
  _4_bit_counter u_4_bit_counter_6 (
    .T__Toggle(clock_1_out), .Reset(and_6_out), .Q3(n4_bit_counter_6_q3), .Q2(n4_bit_counter_6_q2),
    .Q1(n4_bit_counter_6_q1), .Q0(n4_bit_counter_6_q0));

  // Notes on the sheet:
  //   7-segment display
  //   LED Decoder (7-seg driver)
  //   4-bit counter
  //   Time Adjust (HH:MM:SS)
endmodule

module LED_decoder (
  input  I4,
  input  I3,
  input  I2,
  input  I1,
  output o1,
  output o2,
  output o3,
  output o5,
  output o6,
  output o7,
  output o8
);

  wire and_1_out, and_2_out, and_3_out, and_4_out, and_5_out, and_6_out, and_7_out, and_8_out, and_9_out,
       and_10_out, and_11_out, and_12_out, and_13_out, and_14_out, and_15_out, and_16_out, and_17_out,
       and_18_out, and_19_out, and_20_out, and_21_out, and_22_out, and_23_out, and_24_out, and_25_out,
       and_26_out, and_27_out, and_28_out, and_29_out, and_30_out, and_31_out, and_32_out, and_33_out,
       and_34_out, and_35_out, and_36_out, not_1_out, not_2_out, not_3_out, not_4_out, not_5_out, not_6_out,
       not_7_out, not_8_out, not_9_out, not_10_out, not_11_out, not_12_out, not_13_out, not_14_out,
       not_15_out, not_16_out, not_17_out, not_18_out, not_19_out, not_20_out, not_21_out, not_22_out,
       not_23_out, not_24_out, not_25_out, not_26_out, not_27_out, not_28_out, not_29_out, not_30_out,
       not_31_out, not_32_out, not_33_out, not_34_out, not_35_out, not_36_out, not_37_out, not_38_out,
       not_39_out, not_40_out, not_41_out, not_42_out, not_43_out, not_44_out, not_45_out;

  not not_1 (not_1_out, I3);
  and and_1 (and_1_out, not_1_out, not_2_out);
  not not_2 (not_2_out, I1);
  and and_2 (and_2_out, I2, not_3_out);
  not not_3 (not_3_out, I1);
  and and_3 (and_3_out, I4, I2);
  and and_4 (and_4_out, I4, I3);
  not not_4 (not_4_out, I3);
  not not_5 (not_5_out, I2);
  and and_5 (and_5_out, not_4_out, not_5_out, not_6_out);
  not not_6 (not_6_out, I1);
  not not_7 (not_7_out, I4);
  and and_6 (and_6_out, not_7_out, I2, not_8_out);
  not not_8 (not_8_out, I1);
  not not_9 (not_9_out, I3);
  and and_7 (and_7_out, not_9_out, I2, I1);
  and and_8 (and_8_out, I3, not_10_out, I1);
  not not_10 (not_10_out, I2);
  and and_9 (and_9_out, I4, I3, not_11_out);
  not not_11 (not_11_out, I1);
  not not_12 (not_12_out, I3);
  and and_10 (and_10_out, not_12_out, not_13_out);
  not not_13 (not_13_out, I2);
  not not_14 (not_14_out, I3);
  and and_11 (and_11_out, not_14_out, I1);
  not not_15 (not_15_out, I2);
  and and_12 (and_12_out, not_15_out, I1);
  not not_16 (not_16_out, I4);
  and and_13 (and_13_out, not_16_out, I3);
  and and_14 (and_14_out, I4, not_17_out);
  not not_17 (not_17_out, I3);
  not not_18 (not_18_out, I3);
  and and_15 (and_15_out, not_18_out, I2);
  and and_16 (and_16_out, I2, not_19_out);
  not not_19 (not_19_out, I1);
  not not_20 (not_20_out, I4);
  and and_17 (and_17_out, not_20_out, I3, not_21_out);
  not not_21 (not_21_out, I1);
  not not_22 (not_22_out, I2);
  and and_18 (and_18_out, I3, not_22_out, I1);
  and and_19 (and_19_out, I4, not_23_out);
  not not_23 (not_23_out, I3);
  and and_20 (and_20_out, I4, I2);
  not not_24 (not_24_out, I2);
  and and_21 (and_21_out, not_24_out, not_25_out);
  not not_25 (not_25_out, I1);
  not not_26 (not_26_out, I4);
  and and_22 (and_22_out, not_26_out, I3, not_27_out);
  not not_27 (not_27_out, I2);
  and and_23 (and_23_out, I3, not_28_out);
  not not_28 (not_28_out, I1);
  and and_24 (and_24_out, I4, not_29_out);
  not not_29 (not_29_out, I3);
  and and_25 (and_25_out, I4, I2);
  not not_30 (not_30_out, I3);
  and and_26 (and_26_out, not_30_out, not_31_out);
  not not_31 (not_31_out, I1);
  not not_32 (not_32_out, I4);
  and and_27 (and_27_out, not_32_out, I2, I1);
  not not_33 (not_33_out, I4);
  and and_28 (and_28_out, not_33_out, I3, I1);
  and and_29 (and_29_out, I3, I2, I1);
  not not_34 (not_34_out, I3);
  and and_30 (and_30_out, I4, not_34_out, not_35_out);
  not not_35 (not_35_out, I2);
  and and_31 (and_31_out, I4, not_36_out);
  not not_36 (not_36_out, I1);
  not not_37 (not_37_out, I4);
  not not_38 (not_38_out, I2);
  and and_32 (and_32_out, not_37_out, not_38_out, not_39_out);
  not not_39 (not_39_out, I1);
  not not_40 (not_40_out, I3);
  and and_33 (and_33_out, not_40_out, not_41_out);
  not not_41 (not_41_out, I2);
  not not_42 (not_42_out, I3);
  and and_34 (and_34_out, not_42_out, not_43_out);
  not not_43 (not_43_out, I1);
  not not_44 (not_44_out, I4);
  and and_35 (and_35_out, not_44_out, I2, I1);
  not not_45 (not_45_out, I2);
  and and_36 (and_36_out, I4, not_45_out, I1);
  or or_1 (o1, and_1_out, and_2_out, and_3_out, and_4_out);
  or or_2 (o2, and_5_out, and_6_out, and_7_out, and_8_out, and_9_out);
  or or_3 (o3, and_10_out, and_11_out, and_12_out, and_13_out, and_14_out);
  or or_4 (o6, and_21_out, and_22_out, and_23_out, and_24_out, and_25_out);
  or or_5 (o8, and_32_out, and_33_out, and_34_out, and_35_out, and_36_out);
  or or_6 (o5, and_15_out, and_16_out, and_17_out, and_18_out, and_19_out, and_20_out);
  or or_7 (o7, and_26_out, and_27_out, and_28_out, and_29_out, and_30_out, and_31_out);
endmodule

module _4_bit_counter (
  input  T__Toggle,
  input  Reset,
  output Q3,
  output Q2,
  output Q1,
  output Q0
);

  wire t_ff_1_qn, t_ff_2_qn, t_ff_3_qn;

  T_Flip_Flop t_ff_1 (.clk(T__Toggle), .T(1'b1), .Q(Q0), .Qn(t_ff_1_qn), .reset(Reset));  // open: preset, en
  T_Flip_Flop t_ff_2 (.clk(t_ff_1_qn), .T(1'b1), .Q(Q1), .Qn(t_ff_2_qn), .reset(Reset));  // open: preset, en
  T_Flip_Flop t_ff_3 (.clk(t_ff_2_qn), .T(1'b1), .Q(Q2), .Qn(t_ff_3_qn), .reset(Reset));  // open: preset, en
  T_Flip_Flop t_ff_4 (.clk(t_ff_3_qn), .T(1'b1), .Q(Q3), .reset(Reset));  // open: Qn, preset, en

  // Notes on the sheet:
  //   (high)
  //   the more FF are used, the less metastable it is
endmodule
